// Logisim project ALUv0.circ as structural Verilog: 1 circuit, main circuit main
module main (
  input  [3:0] A,
  input  [3:0] B,
  input  [2:0] ALUSelection,
  output Zero,
  output [3:0] ALUout
);

  wire [3:0] adder_1_out, and_1_out, nor_1_out, or_1_out, shifter_1_out, shifter_2_out, subtractor_1_out;

  Adder #(.width(4)) adder_1 (.a(A), .b(B), .out(adder_1_out));  // open: cin, cout
  Subtractor #(.width(4)) subtractor_1 (.a(A), .b(B), .out(subtractor_1_out));  // open: bin, bout
  Shifter #(.width(4)) shifter_1 (.in(A), .\dist (B[1:0]), .out(shifter_1_out));
  Shifter #(.shift("lr"), .width(4)) shifter_2 (.in(A), .\dist (B[1:0]), .out(shifter_2_out));
  assign and_1_out = A & B;  // AND_Gate and_1, 4 bits wide
  assign or_1_out = A | B;  // OR_Gate or_1, 4 bits wide
  assign nor_1_out = ~(A | B);  // NOR_Gate nor_1, 4 bits wide
  Multiplexer #(.select(3), .width(4)) multiplexer_1 (
    .in0(adder_1_out), .in1(subtractor_1_out), .in2(shifter_1_out), .in3(shifter_2_out), .in4(and_1_out),
    .in5(or_1_out), .in6(nor_1_out), .in7(4'b0000), .out(ALUout), .sel(ALUSelection));
  nor nor_2 (Zero, ALUout[0], ALUout[1], ALUout[2], ALUout[3]);
endmodule
