// Logisim project MIPS.circ as structural Verilog: 7 circuits, main circuit main
module main (
  input  [7:0] in_1,
  input  in_2,
  output [3:0] t4,
  output [3:0] t3,
  output [3:0] t2,
  output [3:0] sp,
  output [3:0] t1,
  output [3:0] t0
);

  wire alu_1_zero, clock_1_out, controlunit_1_alusrc, controlunit_1_bne, controlunit_1_branch,
       controlunit_1_jump, controlunit_1_memread, controlunit_1_memtoreg, controlunit_1_memwrite,
       controlunit_1_regdst, controlunit_1_regwrite, multiplexer_3_out;
  wire [2:0] controlunit_1_aluop;
  wire [3:0] alu_1_aluout, datamemory_1_readdata, multiplexer_1_out, multiplexer_5_out, multiplexer_6_out,
       registerfile_1_readdata1, registerfile_1_readdata2;
  wire [7:0] adder_1_out, adder_2_out, bit_extender_1_out, instructionmemory_1_instruction_2,
       multiplexer_2_out, multiplexer_4_out, pc_1_currentaddress;
  wire [15:0] instructionmemory_1_instruction;

  PC pc_1 (.NextAddress(multiplexer_4_out), .Clock(clock_1_out), .Reset(in_2), .CurrentAddress(pc_1_currentaddress));
  Adder adder_1 (.a(pc_1_currentaddress), .b(in_1), .out(adder_1_out));  // open: cin, cout
  InstructionMemory instructionmemory_1 (
    .ReadAddress(pc_1_currentaddress), .Clock(clock_1_out),
    .Instruction({instructionmemory_1_instruction[15:12], instructionmemory_1_instruction_2, instructionmemory_1_instruction[3:0]}));
  ControlUnit controlunit_1 (
    .in_1(instructionmemory_1_instruction[15:12]), .RegWrite(controlunit_1_regwrite),
    .ALUSrc(controlunit_1_alusrc), .MemWrite(controlunit_1_memwrite), .ALUOp(controlunit_1_aluop),
    .MemtoReg(controlunit_1_memtoreg), .MemRead(controlunit_1_memread), .Branch(controlunit_1_branch),
    .RegDst(controlunit_1_regdst), .Jump(controlunit_1_jump), .BNE(controlunit_1_bne));
  Multiplexer #(.width(4)) multiplexer_1 (
    .in0(instructionmemory_1_instruction_2[3:0]), .in1(instructionmemory_1_instruction[3:0]),
    .out(multiplexer_1_out), .sel(controlunit_1_regdst));
  assign bit_extender_1_out = {{4{instructionmemory_1_instruction[3]}}, instructionmemory_1_instruction[3:0]};  // Bit_Extender bit_extender_1
  Clock clock_1 (.out(clock_1_out));
  Adder adder_2 (.a(adder_1_out), .b(bit_extender_1_out), .out(adder_2_out));  // open: cin, cout
  RegisterFile registerfile_1 (
    .RegWrite(controlunit_1_regwrite), .WriteRegisterAddress(multiplexer_1_out),
    .WriteData(multiplexer_6_out), .Reset(in_2), .Clock(clock_1_out),
    .ReadRegisterAddress1(instructionmemory_1_instruction_2[7:4]),
    .ReadRegisterAddress2(instructionmemory_1_instruction_2[3:0]), .sp(sp), .t_4(t4), .t_3(t3), .t_2(t2),
    .t_1(t1), .t_0(t0), .ReadData1(registerfile_1_readdata1), .ReadData2(registerfile_1_readdata2));
  Multiplexer #(.width(8)) multiplexer_2 (
    .in0(adder_1_out), .in1(adder_2_out), .out(multiplexer_2_out), .sel(multiplexer_3_out));
  Multiplexer multiplexer_3 (
    .in0(controlunit_1_bne), .in1(controlunit_1_branch), .out(multiplexer_3_out), .sel(alu_1_zero));
  Multiplexer #(.width(8)) multiplexer_4 (
    .in0(multiplexer_2_out), .in1(instructionmemory_1_instruction_2), .out(multiplexer_4_out),
    .sel(controlunit_1_jump));
  Multiplexer #(.width(4)) multiplexer_5 (
    .in0(registerfile_1_readdata2), .in1(instructionmemory_1_instruction[3:0]), .out(multiplexer_5_out),
    .sel(controlunit_1_alusrc));
  ALU alu_1 (
    .A(registerfile_1_readdata1), .B(multiplexer_5_out), .ALUSelection(controlunit_1_aluop),
    .Zero(alu_1_zero), .ALUout(alu_1_aluout));
  DataMemory datamemory_1 (
    .Address(alu_1_aluout), .MemWrite(controlunit_1_memwrite), .MemRead(controlunit_1_memread),
    .Clock(clock_1_out), .WriteData(registerfile_1_readdata2), .ReadData(datamemory_1_readdata));
  Multiplexer #(.width(4)) multiplexer_6 (
    .in0(alu_1_aluout), .in1(datamemory_1_readdata), .out(multiplexer_6_out), .sel(controlunit_1_memtoreg));

  // Notes on the sheet:
  //   in_1: initial=0x1
endmodule

module RegisterFile (
  input  RegWrite,
  input  [3:0] WriteRegisterAddress,
  input  [3:0] WriteData,
  input  Reset,
  input  Clock,
  input  [3:0] ReadRegisterAddress1,
  input  [3:0] ReadRegisterAddress2,
  output [3:0] sp,
  output [3:0] t_4,
  output [3:0] t_3,
  output [3:0] t_2,
  output [3:0] t_1,
  output [3:0] t_0,
  output [3:0] ReadData1,
  output [3:0] ReadData2
);

  wire decoder_1_out1, decoder_1_out2, decoder_1_out3, decoder_1_out4, decoder_1_out5, decoder_1_out6,
       multiplexer_3_out, not_1_out;
  wire [3:0] multiplexer_4_out;

  not not_1 (not_1_out, Clock);
  Register #(.width(4)) t0 (.D(WriteData), .en(decoder_1_out1), .Q(t_0), .clk(not_1_out), .clr(Reset));
  Multiplexer #(.select(3), .width(4)) multiplexer_1 (
    .in0(4'b0000), .in1(t_0), .in2(t_1), .in3(t_2), .in4(t_3), .in5(t_4), .in6(sp), .out(ReadData1),
    .sel(ReadRegisterAddress1[2:0]));  // open: in7
  Register #(.width(4)) t1 (.D(WriteData), .en(decoder_1_out2), .Q(t_1), .clk(not_1_out), .clr(Reset));
  Decoder #(.select(3)) decoder_1 (
    .out1(decoder_1_out1), .out2(decoder_1_out2), .out3(decoder_1_out3), .out4(decoder_1_out4),
    .out5(decoder_1_out5), .out6(decoder_1_out6), .sel(WriteRegisterAddress[2:0]), .en(RegWrite));  // open: out0, out7
  Register #(.width(4)) t2 (.D(WriteData), .en(decoder_1_out3), .Q(t_2), .clk(not_1_out), .clr(Reset));
  Register #(.width(4)) t3 (.D(WriteData), .en(decoder_1_out4), .Q(t_3), .clk(not_1_out), .clr(Reset));
  Register #(.width(4)) t4 (.D(WriteData), .en(decoder_1_out5), .Q(t_4), .clk(not_1_out), .clr(Reset));
  Multiplexer #(.select(3), .width(4)) multiplexer_2 (
    .in0(4'b0000), .in1(t_0), .in2(t_1), .in3(t_2), .in4(t_3), .in5(t_4), .in6(sp), .out(ReadData2),
    .sel(ReadRegisterAddress2[2:0]));  // open: in7
  Multiplexer multiplexer_3 (.in0(decoder_1_out6), .in1(Reset), .out(multiplexer_3_out), .sel(Reset));
  Multiplexer #(.width(4)) multiplexer_4 (.in0(WriteData), .in1(4'b1111), .out(multiplexer_4_out), .sel(Reset));
  Register #(.width(4)) register_1 (
    .D(multiplexer_4_out), .en(multiplexer_3_out), .Q(sp), .clk(not_1_out));  // open: clr
endmodule

module ALU (
  input  [3:0] A,
  input  [3:0] B,
  input  [2:0] ALUSelection,
  output Zero,
  output [3:0] ALUout
);

  wire [3:0] adder_1_out, and_1_out, nor_1_out, or_1_out, shifter_1_out, shifter_2_out, subtractor_1_out;

  Adder #(.width(4)) adder_1 (.a(A), .b(B), .out(adder_1_out));  // open: cin, cout
  Subtractor #(.width(4)) subtractor_1 (.a(A), .b(B), .out(subtractor_1_out));  // open: bin, bout
  Shifter #(.width(4)) shifter_1 (.in(A), .\dist (B[1:0]), .out(shifter_1_out));
  Shifter #(.shift("lr"), .width(4)) shifter_2 (.in(A), .\dist (B[1:0]), .out(shifter_2_out));
  assign and_1_out = A & B;  // AND_Gate and_1, 4 bits wide
  assign or_1_out = A | B;  // OR_Gate or_1, 4 bits wide
  assign nor_1_out = ~(A | B);  // NOR_Gate nor_1, 4 bits wide
  Multiplexer #(.select(3), .width(4)) multiplexer_1 (
    .in0(adder_1_out), .in1(subtractor_1_out), .in2(shifter_1_out), .in3(shifter_2_out), .in4(and_1_out),
    .in5(or_1_out), .in6(nor_1_out), .in7(4'b0000), .out(ALUout), .sel(ALUSelection));
  nor nor_2 (Zero, ALUout[0], ALUout[1], ALUout[2], ALUout[3]);
endmodule

module InstructionMemory (
  input  [7:0] ReadAddress,
  input  Clock,
  output [15:0] Instruction
);

  wire [7:0] register_1_q;

  Register #(.trigger("falling")) register_1 (.D(ReadAddress), .clk(Clock), .Q(register_1_q));  // open: en, clr
  ROM #(.dataWidth(16)) rom_1 (.addr(register_1_q), .data(Instruction));

  // Notes on the sheet:
  //   contents of rom_1 (hex, n*v repeats v):
  //   b024 b030 b011 5310 b331 332d b030 8340 5640 7661 b331 332b b030 b661 8640 5344 b331 332b b030 b010
  //   8344 1141 b331 332c e131 4302 b043 61d0 b042 414 d403
endmodule

module DataMemory (
  input  [3:0] Address,
  input  MemWrite,
  input  MemRead,
  input  Clock,
  input  [3:0] WriteData,
  output [3:0] ReadData
);

  RAM #(.addrWidth(4), .dataWidth(4)) ram_1 (
    .addr(Address), .we(MemWrite), .oe(MemRead), .clk(Clock), .din(WriteData), .dout(ReadData));
endmodule

module ControlUnit (
  input  [3:0] in_1,
  output RegWrite,
  output ALUSrc,
  output MemWrite,
  output [2:0] ALUOp,
  output MemtoReg,
  output MemRead,
  output Branch,
  output RegDst,
  output Jump,
  output BNE
);

  ROM #(.addrWidth(4), .dataWidth(12)) rom_1 (
    .addr(in_1), .data({BNE, Jump, RegDst, Branch, MemRead, MemtoReg, ALUOp, MemWrite, ALUSrc, RegWrite}));

  // Notes on the sheet:
  //   contents of rom_1 (hex, n*v repeats v):
  //   229 201 209 808 108 6 400 b c3 221 1b 3 2b 231 23 13
endmodule

module PC (
  input  [7:0] NextAddress,
  input  Clock,
  input  Reset,
  output [7:0] CurrentAddress
);

  Register register_1 (.D(NextAddress), .Q(CurrentAddress), .clk(Clock), .clr(Reset));  // open: en
endmodule
